# Fritzing sketch schematic (saved by Fritzing 0.9.5d)
breadboards: 1

parts:
  Part1 = Adafruit PN532 Breakout [part_number="Adafruit #364"]
  Mod1 = Arduino MKR Wifi 1010

nets:
  VDD: Part1.VDD, Mod1.+3V3
  N1: Part1.SCK, Mod1.D9/SCK
  N2: Part1.MISO, Mod1.D10/MISO
  N3: Part1.MOSI/SDA/TX, Mod1.D8/MOSI
  N4: Part1.NSS/SCL/RX, Mod1.~D3
  GND: Part1.GND, Mod1.GND

custom parts:
  Adafruit PN532 Breakout: The PN532 is the most popular NFC chip, and is what is embedded in pretty much every phone or device that does NFC. It can pretty much do it all, such as read and write to tags and cards, communicate with phones (say for payment processing), and 'act' like a NFC tag. If you want to do any sort of embedded NFC work, this is the chip you'll want to use! NFC (Near Field Communications) is a way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
  Arduino MKR Wifi 1010: Arduino MKR Wifi 1010, SAMD21 Cortex-M0+ 32bit Low Power ARM MCU,Flash Memory 256 KB, SRAM 32KB, 48mhz clock, Ublok Wifi interface.
